# Fritzing sketch LM358synth (saved by Fritzing 0.9.3b)
circuit board: 8.46667cm x 5.64444cm
breadboards: 1

parts:
  R5 = Resistor [tolerance=±5% resistance=100k package=THT]
  VCC1 = Battery block 9V
  R4 = Resistor [tolerance=±5% resistance=100k package=THT]
  R1 = Resistor [tolerance=±5% resistance=47k package=THT]
  R2 = Resistor [tolerance=±5% resistance=22k package=THT]
  S1 = Momentary Switch [package=ksa_sealed_tac_switch]
  R3 = Resistor [tolerance=±5% resistance=10k package=THT]
  IC3 = IC, DIP package, 8 pins [chip_label=LM358]
  IC2 = IC, DIP package, 8 pins [chip_label=LM358]
  C2 = Electrolytic Capacitor [capacitance=2.2µF package="100 mil [THT, electrolytic]"]
  R7 = Resistor [tolerance=±5% resistance=22k package=THT]
  R6 = Resistor [tolerance=±5% resistance=47k package=THT]
  R8 = Resistor [tolerance=±5% resistance=470k package=THT]
  R9 = Resistor [tolerance=±5% resistance=100k package=THT]
  R10 = Resistor [tolerance=±5% resistance=100k package=THT]
  IC4 = IC, DIP package, 8 pins [chip_label=LM358]
  IC5 = IC, DIP package, 8 pins [chip_label=LM358]
  C3 = Electrolytic Capacitor [capacitance=1µF package="100 mil [THT, electrolytic]"]
  R31 = Resistor [tolerance=±5% resistance=47k package=THT]
  R12 = Resistor [tolerance=±5% resistance=100k package=THT]
  R11 = Resistor [tolerance=±5% resistance=22k package=THT]
  R14 = Resistor [tolerance=±5% resistance=47k package=THT]
  R15 = Resistor [tolerance=±5% resistance=4.7k package=THT]
  R28 = Resistor [tolerance=±5% resistance=22k package=THT]
  LDR1 = Photocell (LDR) [package=THT]
  LDR2 = Photocell (LDR) [package=THT]
  R24 = Resistor [tolerance=±5% resistance=10k package=THT]
  R25 = Resistor [tolerance=±5% resistance=10k package=THT]
  C4 = Ceramic Capacitor [capacitance="100 nF" package="0603 [SMD, multilayer]"]
  R30 = Resistor [tolerance=±5% resistance=22k package=THT]
  C5 = Ceramic Capacitor [capacitance="100 nF" package="0603 [SMD, multilayer]"]
  R32 = Resistor [tolerance=±5% resistance=10k package=THT]
  R27 = Resistor [tolerance=±5% resistance=100k package=THT]
  R26 = Resistor [tolerance=±5% resistance=100k package=THT]
  C6 = Electrolytic Capacitor [capacitance=1µF package="100 mil [THT, electrolytic]"]
  TRS1 = Audio Jack (TRS) 3.5mm [package="4Ucon 08780 [THT]"]
  R40 = Resistor [tolerance=±5% resistance=22k package=THT]
  R29 = Resistor [tolerance=±5% resistance=390k package=THT]
  C1_0_22uF = Film/Foil Capacitor [capacitance=100nF voltage=35V package="7.5mm [THT, pp]"]
  Pot1 = POT [package=pot_mammoth]
  U1 = LM358 [package=dip08]

nets (from the breadboard view):
  N1: R5.Pin_0, U1.G$1_-IN
  N2: R5.Pin_1, VCC1.-, IC3.pin4, IC2.pin4, R10.Pin_1, IC4.pin4, IC5.pin4, IC5.pin5, R15.Pin_1, R27.Pin_1, TRS1.Sleeve, R40.Pin_1, U1.G$1_V-
  N3: VCC1.+, R4.Pin_0, IC3.pin8, IC2.pin2, IC2.pin5, IC2.pin8, R9.Pin_0, R9.Pin_1, R10.Pin_0, IC4.pin8, IC5.pin8, R26.Pin_0, U1.G$1_V+
  N4: R4.Pin_1, U1.G$2_+IN
  N5: R1.Pin_0, S1.4, U1.G$1_OUT
  N6: R1.Pin_1, R2.Pin_0, U1.G$1_+IN
  N7: R2.Pin_1, C1_0_22uF.+, U1.G$2_OUT
  N8: S1.2, Pot1.E
  N9: R3.Pin_0, C1_0_22uF.-, U1.G$2_-IN
  N10: R3.Pin_1, Pot1.A
  N11: IC3.pin1, R14.Pin_0
  N12: IC3.pin3, IC3.pin7, R11.Pin_0
  N13: IC3.pin6, R12.Pin_1, R11.Pin_1
  N14: IC2.pin1, R6.Pin_0, R8.Pin_0
  N15: IC2.pin3, R7.Pin_0, R6.Pin_1
  N16: IC2.pin6, C2.-, R8.Pin_1
  N17: IC2.pin7, C2.+, R7.Pin_1, R12.Pin_0
  N18: IC4.pin1, IC4.pin2, LDR2.pin_0, LDR2.pin_1, C4.0, C4.1, R29.Pin_1
  N19: IC4.pin3, IC5.pin3, R27.Pin_0, R26.Pin_1
  N20: IC4.pin5, R31.Pin_1
  N21: IC4.pin6, R28.Pin_0, R30.Pin_0
  N22: IC4.pin7, R28.Pin_1, LDR1.pin_1
  N23: IC5.pin1, R30.Pin_1, C5.1, R32.Pin_0
  N24: IC5.pin2, R25.Pin_1, C5.0
  N25: IC5.pin6, IC5.pin7
  N26: C3.-, R31.Pin_0
  N27: C3.+, R14.Pin_1, R15.Pin_0
  N28: LDR1.pin_0, R24.Pin_0
  N29: R32.Pin_1, C6.-
  N30: C6.+, TRS1.Ring, TRS1.Tip, R40.Pin_0
